# Fritzing sketch Reacterino (saved by Fritzing 1.0.2b)
perfboards: 1

parts:
  Bauteil2 = Arduino Nano (Rev3.0)
  LED1 = RGB LED (com. cathode, rgb) [color="Red (633nm)" current=0.030A package="5 mm [THT]"]
  LED3 = LED - 5mm [color="Red (633nm)" current=0.030A package="5 mm [THT]"]
  S1 = Pushbutton [package="[THT]"]
  LED2 = LED - 5mm [color="Red (633nm)" current=30mA package="5 mm [THT]"]
  S2 = Pushbutton [package="[THT]"]
  R2 = Resistor [tolerance=±5% resistance=220 package="0402 [SMD]"]
  R6 = Resistor [tolerance=±5% resistance=220 package="0402 [SMD]"]
  VCC1 = Battery block 9V
  R7 = Resistor [tolerance=±5% power=0.25W resistance=220 package=THT]

nets:
  N1: Bauteil2.GND, LED3.cathode, S1.Pin_1, S1.Pin_2, LED2.cathode, S2.Pin_3, S2.Pin_4, VCC1.-, R7.Pin_0
  N2: Bauteil2.D2, S2.Pin_1, S2.Pin_2
  N3: Bauteil2.D4, R6.Pin_0
  N4: Bauteil2.D8, R2.Pin_0
  N5: Bauteil2.D9, LED1.blue_anode
  N6: Bauteil2.D10, LED1.green_anode
  N7: Bauteil2.D11/MOSI, LED1.red_anode
  N8: Bauteil2.D12/MISO, S1.Pin_3, S1.Pin_4
  N9: Bauteil2.VIN, VCC1.+
  N10: LED1.common_cathode, R7.Pin_1
  N11: LED3.anode, R2.Pin_1
  N12: LED2.anode, R6.Pin_1
